# Fritzing sketch wiring (saved by Fritzing 0.9.3b)
breadboards: 1

parts:
  Bauteil1 = Arduino MKR1000
  Bauteil2 = 9-DOF Absolute Orientation IMU Fusion Breakout - BNO055
  Bauteil3 = 12 NeoPixel Ring [part_number=1643]

nets:
  N1: Bauteil1.D6, Bauteil3.IN
  N2: Bauteil1.D11_SDA, Bauteil2.SDA_5V
  N3: Bauteil1.D12_SCL, Bauteil2.SCL_5V
  GND: Bauteil1.GND, Bauteil2.GND, Bauteil3.GND
  VCC: Bauteil1.VCC, Bauteil2.5.0V, Bauteil3.VDD

custom parts:
  Arduino MKR1000: MKR1000 is a powerful board that combines the functionality of the Zero and the Wi-Fi Shield. It is the ideal solution for makers wanting to design IoT projects with minimal previous experience in networking
  9-DOF Absolute Orientation IMU Fusion Breakout - BNO055: A MEMS accelerometer, magnetometer and gyroscope on a single die with a high speed ARM Cortex-M0 based processor to digest all the sensor data, abstract the sensor fusion and real time requirements away, and spit out data you can use in quaternions, Euler angles or vectors.
  12 NeoPixel Ring: 12 ultra bright smart LED NeoPixels are arranged in a circle with 1.5" (37mm) outer diameter. The rings are 'chainable' - connect the output pin of one to the input pin of another. Use only one microcontroller pin to control as many as you can chain together! Each LED is addressable as the driver chip is inside the LED. Each one has ~18mA constant current drive so the color will be very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
