# Fritzing sketch wiring (saved by Fritzing 0.9.3b)
breadboards: 1

parts:
  Bauteil1 = Arduino MKR1000
  Bauteil2 = 9-DOF Absolute Orientation IMU Fusion Breakout - BNO055

nets:
  N1: Bauteil1.D11_SDA, Bauteil2.SDA_5V
  N2: Bauteil1.D12_SCL, Bauteil2.SCL_5V
  GND: Bauteil1.GND, Bauteil2.GND
  N3: Bauteil1.VCC, Bauteil2.5.0V

custom parts:
  Arduino MKR1000: MKR1000 is a powerful board that combines the functionality of the Zero and the Wi-Fi Shield. It is the ideal solution for makers wanting to design IoT projects with minimal previous experience in networking
  9-DOF Absolute Orientation IMU Fusion Breakout - BNO055: A MEMS accelerometer, magnetometer and gyroscope on a single die with a high speed ARM Cortex-M0 based processor to digest all the sensor data, abstract the sensor fusion and real time requirements away, and spit out data you can use in quaternions, Euler angles or vectors.
